// Logisim project realaluu.circ as structural Verilog
module \and  (
  input  [7:0] a,
  input  [7:0] b,
  output [7:0] out_3
);

  assign out_3 = a & b;  // AND_Gate and_1, 8 bits wide
endmodule

module \or  (
  input  [7:0] a,
  input  [7:0] b,
  output [7:0] out_3
);

  assign out_3 = a | b;  // OR_Gate or_1, 8 bits wide
endmodule

module notb (
  input  [7:0] b,
  output [7:0] out_2
);

  assign out_2 = ~b;  // NOT_Gate not_1, 8 bits wide
endmodule

module LSL (
  input  [7:0] B,
  output [7:0] out_2,
  output Ov
);


  assign out_2 = {B[6:0], 1'b0};
  assign Ov = B[7];
endmodule
